// Logisim project Final_Sem_Project...circ as structural Verilog: 3 circuits, main circuit main
module main (
);

  wire and_4_out, and_5_out, and_6_out, and_12_out, and_13_out, and_14_out, balanceChoice, buffer_1_out,
       buffer_2_out, buffer_3_out, button_1_out, button_2_out, button_4_out, clock_1_out, clock_2_out,
       comparator_2_eq, comparator_2_gt, comparator_2_lt, detect, digitLeft1, digitLeft1B, digitLeft2,
       digitLeft2B, digitLeft3, digitLeft3B, digitLeft4, digitLeft4B, digitLeft5, digitLeft5B, digitLeft6,
       digitLeft6B, digitLeft7, digitLeft7B, dispense, not_1_out, not_2_out, not_3_out, not_4_out, not_5_out,
       not_6_out, not_8_out, not_9_out, not_10_out, not_11_out, not_12_out, not_13_out, not_14_out,
       not_15_out, not_16_out, not_17_out, not_19_out, not_20_out, not_21_out, not_22_out, or_1_out,
       or_2_out, or_3_out, or_4_out, or_5_out, or_7_out, or_8_out, or_9_out, or_10_out, or_11_out, or_13_out,
       or_14_out, or_15_out, or_16_out, or_17_out, or_18_out, or_19_out, or_20_out, or_22_out, or_23_out,
       or_24_out, syilingNOT, syilingNOTB, syilingTrue;
  wire [1:0] adder_1_out, AddressROM;
  wire [3:0] adder_2_out, balance, outAdder, PriceTunnel, subtractor_2_out, valRAM;
  wire [3:1] multiplexer_1_out;

  Multiplexer #(.width(4)) multiplexer_1 (
    .in0(valRAM), .in1(balance), .out({multiplexer_1_out, syilingTrue}), .sel(balanceChoice));
  not not_1 (not_1_out, multiplexer_1_out[3]);
  not not_2 (not_2_out, multiplexer_1_out[2]);
  not not_3 (not_3_out, multiplexer_1_out[1]);
  not not_4 (not_4_out, multiplexer_1_out[3]);
  not not_5 (not_5_out, multiplexer_1_out[2]);
  not not_6 (not_6_out, multiplexer_1_out[1]);
  not not_7 (syilingNOT, syilingTrue);
  or or_1 (or_1_out, not_1_out, multiplexer_1_out[2], multiplexer_1_out[1]);
  or or_2 (or_2_out, not_4_out, multiplexer_1_out[2]);
  not not_8 (not_8_out, multiplexer_1_out[3]);
  not not_9 (not_9_out, multiplexer_1_out[2]);
  not not_10 (not_10_out, multiplexer_1_out[1]);
  and and_1 (digitLeft1, or_1_out, or_3_out);
  or or_3 (or_3_out, multiplexer_1_out[3], multiplexer_1_out[2], not_3_out);
  or or_4 (or_4_out, not_1_out, not_2_out, multiplexer_1_out[1]);
  or or_5 (or_5_out, not_1_out, multiplexer_1_out[2], not_3_out);
  and and_2 (digitLeft3, or_4_out, or_5_out);
  and and_3 (digitLeft5, or_2_out, not_6_out);
  or or_6 (digitLeft6, multiplexer_1_out[3], not_5_out, multiplexer_1_out[1]);
  not not_11 (not_11_out, multiplexer_1_out[3]);
  or or_7 (or_7_out, multiplexer_1_out[3], multiplexer_1_out[2]);
  or or_8 (or_8_out, not_8_out, not_9_out, not_10_out);
  and and_4 (and_4_out, multiplexer_1_out[3], not_2_out);
  and and_5 (and_5_out, multiplexer_1_out[3], not_3_out);
  and and_6 (and_6_out, not_2_out, not_3_out);
  or or_9 (or_9_out, multiplexer_1_out[3], multiplexer_1_out[2], not_6_out);
  or or_10 (or_10_out, not_4_out, not_5_out, not_6_out);
  or or_11 (or_11_out, not_11_out, multiplexer_1_out[2], multiplexer_1_out[1]);
  and and_7 (digitLeft4, or_7_out, or_8_out);
  or or_12 (digitLeft2, and_4_out, and_5_out, and_6_out);
  and and_8 (digitLeft7, or_9_out, or_10_out, or_11_out);
  Clock clock_1 (.out(clock_1_out));
  RAM #(.addrWidth(3), .dataWidth(4)) ram_1 (
    .addr(3'b000), .we(1'b1), .oe(1'b1), .clk(clock_1_out), .din(outAdder), .dout(valRAM));
  ROM #(.addrWidth(2), .dataWidth(4)) rom_1 (.addr(AddressROM), .data(PriceTunnel));
  Adder #(.width(2)) adder_1 (.a(AddressROM), .b(2'b01), .out(adder_1_out));  // open: cin, cout
  Adder #(.width(4)) adder_2 (.a(outAdder), .b(4'b0001), .out(adder_2_out));  // open: cin, cout
  Button button_1 (.out(button_1_out));
  Button button_2 (.out(button_2_out));
  buf buffer_1 (buffer_1_out, dispense);
  Button button_3 (.out(dispense));
  Register #(.width(2)) register_1 (
    .D(adder_1_out), .en(detect), .clk(button_2_out), .Q(AddressROM), .clr(button_4_out));
  Button button_4 (.out(button_4_out));
  Register #(.width(4)) register_2 (.D(adder_2_out), .en(1'b1), .clk(button_1_out), .Q(outAdder), .clr(buffer_3_out));
  buf buffer_2 (buffer_2_out, buffer_1_out);
  buf buffer_3 (buffer_3_out, buffer_2_out);
  Comparator #(.mode("unsigned"), .width(4)) comparator_1 (.a(valRAM), .b(4'b0000), .eq(detect));  // open: gt, lt
  Comparator #(.mode("unsigned"), .width(4)) comparator_2 (
    .a(valRAM), .b(PriceTunnel), .gt(comparator_2_gt), .eq(comparator_2_eq), .lt(comparator_2_lt));
  Subtractor #(.width(4)) subtractor_1 ();  // open: a, b, out, bin, bout
  LedBar #(.matrixcols(1)) ledbar_1 (.led0(or_13_out));
  or or_13 (or_13_out, comparator_2_gt, comparator_2_eq);
  Subtractor #(.width(4)) subtractor_2 (.a(valRAM), .b(PriceTunnel), .out(subtractor_2_out));  // open: bin, bout
  Clock clock_2 (.out(clock_2_out));
  and and_9 (balanceChoice, or_13_out, dispense);
  Register #(.width(4)) register_3 (.D(subtractor_2_out), .en(or_13_out), .clk(clock_2_out), .Q(balance));  // open: clr
  not not_12 (not_12_out, PriceTunnel[3]);
  not not_13 (not_13_out, PriceTunnel[2]);
  not not_14 (not_14_out, PriceTunnel[1]);
  not not_15 (not_15_out, PriceTunnel[3]);
  not not_16 (not_16_out, PriceTunnel[2]);
  not not_17 (not_17_out, PriceTunnel[1]);
  not not_18 (syilingNOTB, PriceTunnel[0]);
  or or_14 (or_14_out, not_15_out, PriceTunnel[2]);
  not not_19 (not_19_out, PriceTunnel[3]);
  not not_20 (not_20_out, PriceTunnel[2]);
  not not_21 (not_21_out, PriceTunnel[1]);
  or or_15 (or_15_out, not_12_out, PriceTunnel[2], PriceTunnel[1]);
  or or_16 (or_16_out, PriceTunnel[3], PriceTunnel[2], not_14_out);
  or or_17 (or_17_out, not_12_out, not_13_out, PriceTunnel[1]);
  or or_18 (or_18_out, not_12_out, PriceTunnel[2], not_14_out);
  and and_10 (digitLeft1B, or_15_out, or_16_out);
  and and_11 (digitLeft5B, or_14_out, not_17_out);
  not not_22 (not_22_out, PriceTunnel[3]);
  or or_19 (or_19_out, PriceTunnel[3], PriceTunnel[2]);
  or or_20 (or_20_out, not_19_out, not_20_out, not_21_out);
  and and_12 (and_12_out, PriceTunnel[3], not_13_out);
  and and_13 (and_13_out, PriceTunnel[3], not_14_out);
  and and_14 (and_14_out, not_13_out, not_14_out);
  and and_15 (digitLeft3B, or_17_out, or_18_out);
  or or_21 (digitLeft6B, PriceTunnel[3], not_16_out, PriceTunnel[1]);
  or or_22 (or_22_out, PriceTunnel[3], PriceTunnel[2], not_17_out);
  or or_23 (or_23_out, not_15_out, not_16_out, not_17_out);
  or or_24 (or_24_out, not_22_out, PriceTunnel[2], PriceTunnel[1]);
  and and_16 (digitLeft4B, or_19_out, or_20_out);
  or or_25 (digitLeft2B, and_12_out, and_13_out, and_14_out);
  and and_17 (digitLeft7B, or_22_out, or_23_out, or_24_out);
  _7_Segment_Display u_7_segment_display_1 (
    .g(digitLeft4), .f(digitLeft2), .a(digitLeft1), .b(digitLeft3), .e(digitLeft5), .d(digitLeft7),
    .c(digitLeft6), .dp(1'b1));
  _7_Segment_Display u_7_segment_display_2 (
    .g(digitLeft4B), .f(digitLeft2B), .a(digitLeft1B), .b(digitLeft3B), .e(digitLeft5B), .d(digitLeft7B),
    .c(digitLeft6B), .dp(1'b1));
  _7_Segment_Display u_7_segment_display_3 (
    .g(syilingTrue), .f(1'b1), .a(1'b1), .b(syilingNOT), .e(syilingNOT), .d(1'b1), .c(1'b1));  // open: dp
  _7_Segment_Display u_7_segment_display_4 (
    .g(PriceTunnel[0]), .f(1'b1), .a(1'b1), .b(syilingNOTB), .e(syilingNOTB), .d(1'b1), .c(1'b1));  // open: dp

  // Other names for the same wires on the sheet: syilingTrueB = PriceTunnel[0]

  // Notes on the sheet:
  //   contents of rom_1 (hex, n*v repeats v):
  //   3 e 7
endmodule

module Assignment_test (
  input  in_1,
  input  in_2,
  input  in_3,
  input  in_4,
  input  in_5,
  input  in_6,
  input  A,
  input  B,
  input  C,
  input  D,
  input  in_11,
  input  in_12,
  input  in_13,
  input  in_14
);

  wire and_1_out, and_2_out, and_3_out, and_4_out, and_5_out, and_6_out, and_7_out, nand_1_out, nand_2_out,
       nand_3_out, nand_4_out, nand_5_out, nand_6_out, nand_7_out, nand_8_out, nand_9_out, nand_10_out,
       nor_1_out, nor_2_out, nor_3_out, nor_4_out, nor_5_out, nor_6_out, nor_7_out, not_1_out, not_2_out,
       not_3_out, not_4_out, not_5_out, not_6_out, not_7_out, not_8_out, not_9_out, or_1_out, or_2_out,
       or_3_out, or_4_out, undriven, undriven_2, undriven_3;

  or or_1 (or_1_out, A, C);
  not not_1 (not_1_out, A);
  and and_1 (and_1_out, undriven, not_4_out, not_6_out);
  not not_2 (not_2_out, undriven);
  LED led_1 (.in(and_2_out));
  and and_2 (and_2_out, or_1_out, or_2_out, or_4_out);
  or or_2 (or_2_out, not_1_out, not_3_out, C);
  not not_3 (not_3_out, B);
  LED led_2 (.in(or_3_out));
  or or_3 (or_3_out, and_1_out, and_3_out, and_4_out);
  and and_3 (and_3_out, not_2_out, not_4_out, undriven_3);
  not not_4 (not_4_out, undriven_2);
  not not_5 (not_5_out, C);
  and and_4 (and_4_out, undriven, undriven_2);
  not not_6 (not_6_out, undriven_3);
  or or_4 (or_4_out, not_1_out, not_5_out, D);
  and and_5 (and_5_out, in_1, not_8_out, not_9_out);
  not not_7 (not_7_out, in_1);
  nand nand_1 (nand_1_out, and_5_out, and_6_out, and_7_out);
  LED led_3 (.in(nand_1_out));
  and and_6 (and_6_out, not_7_out, not_8_out, in_3);
  not not_8 (not_8_out, in_2);
  and and_7 (and_7_out, in_1, in_2);
  not not_9 (not_9_out, in_3);
  nor nor_1 (nor_1_out, in_12, in_14);
  nor nor_2 (nor_2_out, in_12, in_12);
  nor nor_3 (nor_3_out, nor_2_out, nor_4_out, in_14);
  nor nor_4 (nor_4_out, in_13, in_13);
  nand nand_2 (nand_2_out, in_4, nand_8_out, nand_10_out);
  not nand_3 (nand_3_out, in_4);  // NAND_Gate
  LED led_4 (.in(nor_5_out));
  nor nor_5 (nor_5_out, nor_1_out, nor_3_out, nor_7_out);
  nor nor_6 (nor_6_out, in_14, in_14);
  LED led_5 (.in(nand_4_out));
  nand nand_4 (nand_4_out, nand_5_out, nand_9_out);
  nand nand_5 (nand_5_out, nand_6_out, nand_6_out);
  nand nand_6 (nand_6_out, nand_2_out, nand_7_out);
  nand nand_7 (nand_7_out, nand_3_out, nand_8_out, in_6);
  nor nor_7 (nor_7_out, nor_2_out, nor_6_out, in_11);
  not nand_8 (nand_8_out, in_5);  // NAND_Gate
  nand nand_9 (nand_9_out, in_4, in_5);
  not nand_10 (nand_10_out, in_6);  // NAND_Gate
endmodule

module lmfao (
);

  main main_1 ();
endmodule
